# Fritzing sketch noodle (saved by Fritzing 1.0.6)
circuit board: 3.99999cm x 11cm
breadboards: 2

parts:
  100K1 = Rotary Potentiometer (Small) [maximum_resistance=100kΩ knob_status=50% power=0.5W package=THT]
  100K2 = Rotary Potentiometer (Small) [maximum_resistance=100kΩ knob_status=50% power=0.5W package=THT]
  100K0 = Rotary Potentiometer (Small) [maximum_resistance=100kΩ knob_status=50% power=0.5W package=THT]
  CLK = PJ-301M [part_number=PJ-301M]
  104 = Ceramic Capacitor [capacitance=100nF voltage=16V package="200 mil [THT, multilayer]"]
  rec = PJ-301M [part_number=PJ-301M]
  IN2 = PJ-301M [part_number=PJ-301M]
  ~ = PJ-301M [part_number=PJ-301M]
  10k = Resistor [tolerance=±1% resistance=10k power=0.25W package=THT]
  1K2 = Resistor [tolerance=±5% resistance=1k power=0.25W package=THT]
  4_7uF = Electrolytic Capacitor [capacitance=4.7µF voltage=35V package="100 mil [THT, electrolytic]"]  # not connected
  4_7uF_2 = Electrolytic Capacitor [capacitance=4.7µF voltage=35V package="100 mil [THT, electrolytic]"]  # not connected
  103 = Ceramic Capacitor [capacitance=10nF voltage=16V package="200 mil [THT, multilayer]"]
  103_2 = Ceramic Capacitor [capacitance=10nF voltage=16V package="200 mil [THT, multilayer]"]
  J3 = shrouded pin header, 16 pins [form="♂ (shrouded male)"]
  100K4 = Rotary Potentiometer (Small) [maximum_resistance=100kΩ knob_status=50% power=0.5W package=THT]
  100K6 = Rotary Potentiometer (Small) [maximum_resistance=100kΩ knob_status=50% power=0.5W package=THT]
  4051B = IC, DIP package, 16 pins [chip_label=4051]
  100uF = Electrolytic Capacitor [capacitance=0.1mF voltage=35V package="100 mil [THT, electrolytic]"]
  40106 = 40106 DIP - 14 pins [chip_label=40106 package="DIP (Dual Inline) [THT]"]
  CD4015 = IC, DIP package, 16 pins [chip_label=4015B]
  5||15 = SPST Switch [package=switch-spdt_kit]
  5817 = Schottky Diode [part_number=1N5817 package="300 mil [THT]"]
  4051B1 = IC, DIP package, 16 pins [chip_label=4051]
  103_3 = Ceramic Capacitor [capacitance=10nF voltage=16V package="200 mil [THT, multilayer]"]
  103_4 = Ceramic Capacitor [capacitance=10nF voltage=16V package="200 mil [THT, multilayer]"]
  rec+ = Pushbutton [package="[THT]"]
  rec- = Pushbutton [package="[THT]"]
  LED2 = LED - 3mm [color="Blue (430nm)" current=0.030A package="3 mm [THT]"]
  1K1 = Resistor [tolerance=±5% resistance=1k power=0.25W package=THT]
  1K0 = Resistor [tolerance=±5% resistance=1k power=0.25W package=THT]
  LED1 = LED - 3mm [color="Blue (430nm)" current=0.030A package="3 mm [THT]"]
  LED0 = LED - 3mm [color="Blue (430nm)" current=0.030A package="3 mm [THT]"]
  LED4 = LED - 3mm [color="Blue (430nm)" current=0.030A package="3 mm [THT]"]
  LED6 = LED - 3mm [color="Blue (430nm)" current=0.030A package="3 mm [THT]"]
  1K4 = Resistor [tolerance=±5% resistance=470k power=0.25W package=THT]
  1K6 = Resistor [tolerance=±5% resistance=1k power=0.25W package=THT]
  100k = Rotary Potentiometer (Small) [maximum_resistance=100kΩ knob_status=50% power=0.5W package=THT]  # not connected

nets:
  GND: 100K1.leg1, 100K2.leg1, 100K0.leg1, CLK.Pin_1, 104.0, rec.Pin_1, IN2.Pin_1, ~.Pin_1, 103.0, 103_2.1, J3.pin2, J3.pin3, J3.pin4, J3.pin13, J3.pin14, J3.pin15, 100K4.leg1, 100K6.leg1, 4051B.pin6, 4051B.pin8, 100uF.-, 40106.pin7, CD4015.pin6, CD4015.pin8, CD4015.pin14, 4051B1.pin6, 4051B1.pin8, 103_3.1, 103_4.0, rec-.Pin_3, rec-.Pin_4, LED2.cathode, LED1.cathode, LED0.cathode, LED4.cathode, LED6.cathode
  N1: 100K1.wiper, 4051B.pin14
  9V/vdd: 100K1.leg2, 100K2.leg2, 100K0.leg2, 104.1, 103.1, 103_2.0, J3.pin5, J3.pin6, J3.pin11, J3.pin12, 100K4.leg2, 100K6.leg2, 4051B.pin16, 100uF.+, 40106.pin14, CD4015.pin16, 4051B1.pin3, 4051B1.pin16, 103_3.0, 103_4.1, rec+.Pin_3, rec+.Pin_4
  N2: 100K2.wiper, 4051B.pin13
  N3: 100K0.wiper, 4051B.pin15
  N4: CLK.Pin_3, 40106.pin10
  N5: rec.Pin_3, 40106.pin12
  N6: ~.Pin_3, 5817.cathode
  N7: 10k.Pin_0, CD4015.pin7, 5||15.P, rec+.Pin_1, rec+.Pin_2, rec-.Pin_1, rec-.Pin_2
  N8: 10k.Pin_1, CD4015.pin2
  N9: 1K2.Pin_0, 4051B1.pin15
  N10: 1K2.Pin_1, LED2.anode
  N11: J3.pin1, J3.pin16
  N12: J3.pin7, J3.pin10
  N13: J3.pin8, J3.pin9
  N14: 100K4.wiper, 4051B.pin1
  N15: 100K6.wiper, 4051B.pin2
  N16: 4051B.pin3, 5817.anode
  C: 4051B.pin9, CD4015.pin11, 4051B1.pin9
  B: 4051B.pin10, CD4015.pin4, 4051B1.pin10
  A: 4051B.pin11, CD4015.pin5, 4051B1.pin11
  N17: 40106.pin11, CD4015.pin1, CD4015.pin9
  N18: 40106.pin13, 5||15.O
  N19: CD4015.pin10, CD4015.pin15
  N20: 4051B1.pin1, 1K4.Pin_1
  N21: 4051B1.pin2, 1K6.Pin_1
  N22: 4051B1.pin13, 1K0.Pin_0
  N23: 4051B1.pin14, 1K1.Pin_0
  N24: 1K1.Pin_1, LED1.anode
  N25: 1K0.Pin_1, LED0.anode
  N26: LED4.anode, 1K4.Pin_0
  N27: LED6.anode, 1K6.Pin_0

notes:
  noodle
  blueprint@poetaster . de 2026
  jlcjlcjlcjlc

custom parts:
  PJ-301M: Phone power jack.
  40106 DIP - 14 pins: A DIP stand-in part for whatever IC you want. With 14 pins on a 300mil dual inline package (DIP) footprint.
